# Fritzing sketch esquema_led (saved by Fritzing 1.0.6)
breadboards: 1

parts:
  Componente1 = Arduino Uno (Rev3)
  LED1 = LED - 5mm [color="Red (633nm)" current=0.030A package="5 mm [THT]"]

nets:
  N1: Componente1.D13/SCK, LED1.anode
  N2: Componente1.GND, LED1.cathode
